# Fritzing sketch ArduinoISP_UNOR3 (saved by Fritzing 0.9.3b)
breadboards: 1

parts:
  Componente3 = Arduino Nano (Rev3.0) (ICSP)
  Componente4 = Arduino Uno (Rev3) - ICSP

nets:
  GND: Componente3.GND, Componente4.GND
  N1: Componente3.D10, Componente4.RESET
  N2: Componente3.D11/MOSI, Componente4.D11_PWM/MOSI
  N3: Componente3.D12/MISO, Componente4.ICSP_MISO, Componente4.D12/MISO
  5V: Componente3.5V, Componente4.5V
  N4: Componente3.D13/SCK, Componente4.D13/SCK
